# Fritzing sketch ESQUEMA_EMISOR (saved by Fritzing 0.9.10b)

parts:
  DHT1 = Humidity and Temperature Sensor DHT11
  Componente1 = Arduino Uno (Rev3)
  Componente2 = NRF24L01+ Breakout Board

nets:
  N1: DHT1.Vcc, Componente1.D2
  N2: DHT1.Data-signal, Componente1.5V
  GND: DHT1.GND_2, Componente1.GND, Componente2.GND
  N3: Componente1.D9_PWM, Componente2.CE
  N4: Componente1.D10_PWM/SS, Componente2.CS
  N5: Componente1.D11_PWM/MOSI, Componente2.MOSI
  N6: Componente1.D12/MISO, Componente2.MISO
  N7: Componente1.D13/SCK, Componente2.SCK
  3V3: Componente1.3V3, Componente2.VCC

custom parts:
  Humidity and Temperature Sensor DHT11: Digital relative humidity & temperature sensor DHT11
