# Fritzing sketch ESQUEMA_RECEPTOR (saved by Fritzing 0.9.10b)

parts:
  Componente1 = Arduino Mega 2560 (Rev3)-TopMount
  Componente2 = NRF24L01+ Breakout Board
  Display1 = LCD screen 16x2 IIC [part_number=101290]

nets:
  N1: Componente1.SCL, Display1.SCL
  N2: Componente1.SDA, Display1.SDA
  GND: Componente1.GND, Componente2.GND, Display1.GND
  N3: Componente1.D9_PWM, Componente2.CE
  3V3: Componente1.3V3, Componente2.VCC
  5V: Componente1.5V, Display1.VCC
  N4: Componente1.D50, Componente2.MISO
  N5: Componente1.D51, Componente2.MOSI
  N6: Componente1.D52, Componente2.SCK
  N7: Componente1.D53, Componente2.CS

custom parts:
  Arduino Mega 2560 (Rev3)-TopMount: Arduino Mega 2560 (Rev3) for Top PCB Mount. The PCB view of the Arduino Mega 2560 (Rev3) in Arduino Bin flipped upside down with the text flipped back so as to be readable. Other views haven't changed Protruding component position is outlined to provide indication of part contact. Number in component outline is mm of protrusion of the component from the Mega PCB. Subtract the number from the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
  LCD screen 16x2 IIC: LCD screen with HD44780 controller enables showing text, symbols, value or anything else that comes from Croduino/Arduino. It is capable of showing 16 symbols in two lines and therefore can be used in many projects that need to send clearly visible and legible output information.. • Color of symbols: White • Backlight: Blue • Dimensions: 80 x 36 x 12 mm • Screen dimensions: 64.5 x 16 mm •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
